// Logisim project PongV2.circ as structural Verilog: 2 circuits, main circuit main
module main (
);

  wire and_3_out, and_4_out, and_5_out, button_2_out, button_3_out, button_4_out, button_5_out, cdm_8_1_p2,
       cdm_8_1_p4, cdm_8_1_p5, cdm_8_1_p6, cdm_8_1_p7, cdm_8_1_p8, cdm_8_1_p9, cdm_8_1_p10, Clk, Code,
       comparator_1_eq, comparator_1_gt, comparator_1_lt, comparator_2_eq, comparator_2_gt, comparator_2_lt,
       comparator_3_eq, comparator_3_gt, comparator_3_lt, comparator_4_eq, comparator_4_gt, comparator_4_lt,
       data, decoder_2_out0, decoder_2_out1, decoder_3_out1, decoder_4_out0, decoder_7_out0, decoder_10_out0,
       decoder_11_out0, decoder_12_out0, decoder_15_out0, IO_F8_out, IO_FA_out, IO_FB_out, IO_FC_out,
       IO_FD_out, IO_FE_out, IO_FF_out, mem, nand_1_out, nor_1_out, nor_2_out, not_1_out, not_2_out,
       not_3_out, not_4_out, not_5_out, not_6_out, not_7_out, or_3_out, or_4_out, or_6_out, or_8_out,
       or_9_out, RAM, Rd_Wr, Reset, transistor_1_out;
  wire [3:0] I_O_Adr, LScore, register_1_q, register_1_q_2, RScore;
  wire [6:0] Keyboard;
  wire [7:0] cdm_8_1_p14, cdm_8_1_p15, controlled_buffer_4_out, controlled_buffer_8_out,
       controlled_buffer_12_out, controlled_buffer_13_out, controlled_buffer_16_out,
       controlled_buffer_17_out, I_O_Dat, register_2_q, shifter_1_out, shifter_4_out, shifter_7_out,
       shifter_8_out;
  wire [7:4] cdm_8_1_p13, controlled_buffer_14_out, controlled_buffer_15_out;
  wire [7:7] rs_latch_1_p3;
  wire [15:0] decoder_5_out0, decoder_6_out0, decoder_8_out0, decoder_9_out0;
  wire [31:0] BallX, BallY, LPad, multiplexer_1_out, multiplexer_2_out, multiplexer_3_out, multiplexer_4_out,
       multiplexer_5_out, multiplexer_6_out, multiplexer_7_out, multiplexer_8_out, multiplexer_9_out,
       multiplexer_10_out, multiplexer_11_out, multiplexer_12_out, multiplexer_13_out, multiplexer_14_out,
       multiplexer_15_out, multiplexer_16_out, multiplexer_17_out, multiplexer_18_out, multiplexer_19_out,
       multiplexer_20_out, multiplexer_21_out, multiplexer_22_out, multiplexer_23_out, multiplexer_24_out,
       multiplexer_25_out, multiplexer_26_out, multiplexer_27_out, multiplexer_28_out, multiplexer_29_out,
       multiplexer_30_out, multiplexer_31_out, multiplexer_32_out, or_1_out, or_2_out, RPad, shifter_2_out,
       shifter_3_out, shifter_5_out, shifter_6_out;

  Multiplexer #(.width(32), .enable("false")) multiplexer_1 (
    .in0({32{1'b0}}), .in1(BallY), .out(multiplexer_1_out), .sel(BallX[31]));
  Multiplexer #(.width(32), .enable("false")) multiplexer_2 (
    .in0({32{1'b0}}), .in1(BallY), .out(multiplexer_2_out), .sel(BallX[30]));
  Multiplexer #(.width(32), .enable("false")) multiplexer_3 (
    .in0({32{1'b0}}), .in1(BallY), .out(multiplexer_3_out), .sel(BallX[29]));
  Multiplexer #(.width(32), .enable("false")) multiplexer_4 (
    .in0({32{1'b0}}), .in1(BallY), .out(multiplexer_4_out), .sel(BallX[28]));
  Keyboard keyboard_1 (.clk(Clk), .data(Keyboard));  // open: re, clr, avail
  Multiplexer #(.width(32), .enable("false")) multiplexer_5 (
    .in0({32{1'b0}}), .in1(BallY), .out(multiplexer_5_out), .sel(BallX[27]));
  Multiplexer #(.width(32), .enable("false")) multiplexer_6 (
    .in0({32{1'b0}}), .in1(BallY), .out(multiplexer_6_out), .sel(BallX[25]));
  Multiplexer #(.width(32), .enable("false")) multiplexer_7 (
    .in0({32{1'b0}}), .in1(BallY), .out(multiplexer_7_out), .sel(BallX[26]));
  Multiplexer #(.width(32), .enable("false")) multiplexer_8 (
    .in0({32{1'b0}}), .in1(BallY), .out(multiplexer_8_out), .sel(BallX[24]));
  Multiplexer #(.width(32), .enable("false")) multiplexer_9 (
    .in0({32{1'b0}}), .in1(BallY), .out(multiplexer_9_out), .sel(BallX[22]));
  Multiplexer #(.width(32), .enable("false")) multiplexer_10 (
    .in0({32{1'b0}}), .in1(BallY), .out(multiplexer_10_out), .sel(BallX[23]));
  Hex_Digit_Display hex_digit_display_1 (.value(LScore));  // open: dp
  Multiplexer #(.width(32), .enable("false")) multiplexer_11 (
    .in0({32{1'b0}}), .in1(BallY), .out(multiplexer_11_out), .sel(BallX[21]));
  Multiplexer #(.width(32), .enable("false")) multiplexer_12 (
    .in0({32{1'b0}}), .in1(BallY), .out(multiplexer_12_out), .sel(BallX[20]));
  DotMatrix #(.matrixcols(32), .matrixrows(32)) dotmatrix_1 (
    .col0(or_1_out), .col1(multiplexer_2_out), .col2(multiplexer_3_out), .col3(multiplexer_4_out),
    .col4(multiplexer_5_out), .col5(multiplexer_7_out), .col6(multiplexer_6_out), .col7(multiplexer_8_out),
    .col8(multiplexer_10_out), .col9(multiplexer_9_out), .col10(multiplexer_11_out),
    .col11(multiplexer_12_out), .col12(multiplexer_13_out), .col13(multiplexer_15_out),
    .col14(multiplexer_14_out), .col15(multiplexer_16_out), .col16(multiplexer_18_out),
    .col17(multiplexer_17_out), .col18(multiplexer_20_out), .col19(multiplexer_19_out),
    .col20(multiplexer_21_out), .col21(multiplexer_23_out), .col22(multiplexer_22_out),
    .col23(multiplexer_24_out), .col24(multiplexer_25_out), .col25(multiplexer_26_out),
    .col26(multiplexer_28_out), .col27(multiplexer_27_out), .col28(multiplexer_29_out),
    .col29(multiplexer_30_out), .col30(multiplexer_31_out), .col31(or_2_out));
  assign or_1_out = LPad | multiplexer_1_out;  // OR_Gate or_1, 32 bits wide
  Multiplexer #(.width(32), .enable("false")) multiplexer_13 (
    .in0({32{1'b0}}), .in1(BallY), .out(multiplexer_13_out), .sel(BallX[19]));
  Multiplexer #(.width(32), .enable("false")) multiplexer_14 (
    .in0({32{1'b0}}), .in1(BallY), .out(multiplexer_14_out), .sel(BallX[17]));
  Multiplexer #(.width(32), .enable("false")) multiplexer_15 (
    .in0({32{1'b0}}), .in1(BallY), .out(multiplexer_15_out), .sel(BallX[18]));
  Multiplexer #(.width(32), .enable("false")) multiplexer_16 (
    .in0({32{1'b0}}), .in1(BallY), .out(multiplexer_16_out), .sel(BallX[16]));
  Multiplexer #(.width(32), .enable("false")) multiplexer_17 (
    .in0({32{1'b0}}), .in1(BallY), .out(multiplexer_17_out), .sel(BallX[14]));
  Multiplexer #(.width(32), .enable("false")) multiplexer_18 (
    .in0({32{1'b0}}), .in1(BallY), .out(multiplexer_18_out), .sel(BallX[15]));
  Hex_Digit_Display hex_digit_display_2 (.value(RScore));  // open: dp
  assign or_2_out = RPad | multiplexer_32_out;  // OR_Gate or_2, 32 bits wide
  Multiplexer #(.width(32), .enable("false")) multiplexer_19 (
    .in0({32{1'b0}}), .in1(BallY), .out(multiplexer_19_out), .sel(BallX[12]));
  Multiplexer #(.width(32), .enable("false")) multiplexer_20 (
    .in0({32{1'b0}}), .in1(BallY), .out(multiplexer_20_out), .sel(BallX[13]));
  // Probe on cdm_8_1_p2
  // Probe on cdm_8_1_p4
  Button button_1 (.out(Reset));
  Clock clock_1 (.out(Clk));
  Multiplexer #(.width(32), .enable("false")) multiplexer_21 (
    .in0({32{1'b0}}), .in1(BallY), .out(multiplexer_21_out), .sel(BallX[11]));
  // Probe on cdm_8_1_p7
  // Probe on cdm_8_1_p5
  // Probe on cdm_8_1_p6
  and and_1 (I_O_Adr[0], not_2_out, Clk, data);
  Multiplexer #(.width(32), .enable("false")) multiplexer_22 (
    .in0({32{1'b0}}), .in1(BallY), .out(multiplexer_22_out), .sel(BallX[9]));
  Multiplexer #(.width(32), .enable("false")) multiplexer_23 (
    .in0({32{1'b0}}), .in1(BallY), .out(multiplexer_23_out), .sel(BallX[10]));
  // Probe on cdm_8_1_p9
  // Probe on cdm_8_1_p8
  Multiplexer #(.width(32), .enable("false")) multiplexer_24 (
    .in0({32{1'b0}}), .in1(BallY), .out(multiplexer_24_out), .sel(BallX[8]));
  Decoder #(.disabled(0)) decoder_1 (.out0(Code), .out1(data), .sel(cdm_8_1_p10), .en(mem));
  not not_1 (not_1_out, Rd_Wr);
  // CdM_8 cdm_8_1: pin names not known; wires that end beside it: Clk, cdm_8_1_p2, Reset, cdm_8_1_p4, cdm_8_1_p5, cdm_8_1_p6, cdm_8_1_p7, cdm_8_1_p8, cdm_8_1_p9, cdm_8_1_p10, mem, Rd_Wr, {cdm_8_1_p13, I_O_Adr}, cdm_8_1_p14, cdm_8_1_p15
  assign I_O_Dat = not_1_out ? cdm_8_1_p14 : 8'bz;  // Controlled_Buffer controlled_buffer_1
  assign cdm_8_1_p15 = Rd_Wr ? I_O_Dat : 8'bz;  // Controlled_Buffer controlled_buffer_2
  not not_2 (not_2_out, nand_1_out);
  nand nand_1 (nand_1_out, cdm_8_1_p13[7], cdm_8_1_p13[6], cdm_8_1_p13[5], cdm_8_1_p13[4]);
  and and_2 (RAM, nand_1_out, data);
  Multiplexer #(.width(32), .enable("false")) multiplexer_25 (
    .in0({32{1'b0}}), .in1(BallY), .out(multiplexer_25_out), .sel(BallX[7]));
  Multiplexer #(.width(32), .enable("false")) multiplexer_26 (
    .in0({32{1'b0}}), .in1(BallY), .out(multiplexer_26_out), .sel(BallX[6]));
  Multiplexer #(.width(32), .enable("false")) multiplexer_27 (
    .in0({32{1'b0}}), .in1(BallY), .out(multiplexer_27_out), .sel(BallX[4]));
  Multiplexer #(.width(32), .enable("false")) multiplexer_28 (
    .in0({32{1'b0}}), .in1(BallY), .out(multiplexer_28_out), .sel(BallX[5]));
  // Probe on {cdm_8_1_p13, I_O_Adr}
  Multiplexer #(.width(32), .enable("false")) multiplexer_29 (
    .in0({32{1'b0}}), .in1(BallY), .out(multiplexer_29_out), .sel(BallX[3]));
  ROM rom_1 (.addr({cdm_8_1_p13, I_O_Adr}), .data(I_O_Dat), .sel(Code));
  RAM ram_1 (.addr({cdm_8_1_p13, I_O_Adr}), .data(I_O_Dat), .sel(RAM), .clk(Clk), .ld(Rd_Wr));  // open: clr
  Multiplexer #(.width(32), .enable("false")) multiplexer_30 (
    .in0({32{1'b0}}), .in1(BallY), .out(multiplexer_30_out), .sel(BallX[2]));
  Multiplexer #(.width(32), .enable("false")) multiplexer_31 (
    .in0({32{1'b0}}), .in1(BallY), .out(multiplexer_31_out), .sel(BallX[1]));
  Multiplexer #(.width(32), .enable("false")) multiplexer_32 (
    .in0({32{1'b0}}), .in1(BallY), .out(multiplexer_32_out), .sel(BallX[0]));
  // Probe on I_O_Dat
  Decoder #(.disabled(0)) decoder_2 (.out0(decoder_2_out0), .out1(decoder_2_out1), .sel(Rd_Wr), .en(and_3_out));
  and and_3 (and_3_out, I_O_Adr[0], I_O_Adr[0], I_O_Adr[1], ~I_O_Adr[2], ~I_O_Adr[3]);  // AND_Gate
  Hex_Digit_Display hex_digit_display_3 (.value(register_1_q));  // open: dp
  Register register_1 (.D(I_O_Dat), .Q({register_1_q, register_1_q_2}), .clk(decoder_2_out0));  // open: en, clr
  Hex_Digit_Display hex_digit_display_4 (.value(register_1_q_2));  // open: dp
  assign I_O_Dat = decoder_2_out1 ? {rs_latch_1_p3[7], register_2_q[6:0]} : 8'bz;  // Controlled_Buffer controlled_buffer_3
  Button button_2 (.out(button_2_out));
  assign controlled_buffer_4_out = button_2_out ? 8'h61 : 8'bz;  // Controlled_Buffer controlled_buffer_4
  not not_3 (not_3_out, transistor_1_out);
  not not_4 (not_4_out, decoder_2_out1);
  Button button_3 (.out(button_3_out));
  Transistor #(.\type ("n")) transistor_1 (.in(1'b0), .out(transistor_1_out), .gate(button_2_out));
  Transistor #(.\type ("n")) transistor_2 (.in(1'b0), .out(transistor_1_out), .gate(button_3_out));
  assign controlled_buffer_4_out = button_3_out ? 8'h62 : 8'bz;  // Controlled_Buffer controlled_buffer_5
  nor nor_1 (nor_1_out, transistor_1_out, not_3_out);
  nor nor_2 (nor_2_out, decoder_2_out1, not_4_out);
  Button button_4 (.out(button_4_out));
  Transistor #(.\type ("n")) transistor_3 (.in(1'b0), .out(transistor_1_out), .gate(button_4_out));
  assign controlled_buffer_4_out = button_4_out ? 8'h63 : 8'bz;  // Controlled_Buffer controlled_buffer_6
  // RS_latch rs_latch_1: pin names not known; wires that end beside it: nor_1_out, nor_2_out, rs_latch_1_p3[7]
  Button button_5 (.out(button_5_out));
  Transistor #(.\type ("n")) transistor_4 (.in(1'b0), .out(transistor_1_out), .gate(button_5_out));
  assign controlled_buffer_4_out = button_5_out ? 8'h64 : 8'bz;  // Controlled_Buffer controlled_buffer_7
  Pull_Resistor #(.pull(1)) pull_resistor_1 (.node(transistor_1_out));
  not not_5 (not_5_out, transistor_1_out);
  not not_6 (not_6_out, not_5_out);
  Register #(.trigger("falling")) register_2 (
    .D(controlled_buffer_4_out), .Q(register_2_q), .clk(not_6_out));  // open: en, clr
  not not_7 (not_7_out, or_3_out);
  or or_3 (or_3_out, and_4_out, and_5_out);
  assign controlled_buffer_8_out = not_7_out ? {8{1'b0}} : 8'bz;  // Controlled_Buffer controlled_buffer_8
  and and_4 (and_4_out, Keyboard[6], Keyboard[5], Keyboard[4], ~Keyboard[3], Keyboard[2], Keyboard[1], Keyboard[0]);  // AND_Gate
  and and_5 (and_5_out, Keyboard[6], Keyboard[5], Keyboard[4], ~Keyboard[3], ~Keyboard[2], Keyboard[1], Keyboard[0]);  // AND_Gate
  // Probe on controlled_buffer_8_out
  assign controlled_buffer_8_out = and_4_out ? 8'h1 : 8'bz;  // Controlled_Buffer controlled_buffer_9
  assign controlled_buffer_8_out = and_5_out ? 8'h2 : 8'bz;  // Controlled_Buffer controlled_buffer_10
  assign I_O_Dat = decoder_3_out1 ? controlled_buffer_8_out : 8'bz;  // Controlled_Buffer controlled_buffer_11
  and IO_F8 (IO_F8_out, I_O_Adr[0], ~I_O_Adr[0], ~I_O_Adr[1], ~I_O_Adr[2], I_O_Adr[3]);  // AND_Gate
  Decoder #(.disabled(0)) decoder_3 (.out1(decoder_3_out1), .sel(Rd_Wr), .en(IO_F8_out));  // open: out0
  assign controlled_buffer_12_out = decoder_4_out0 ? I_O_Dat : 8'bz;  // Controlled_Buffer controlled_buffer_12
  and IO_FA (IO_FA_out, I_O_Adr[0], ~I_O_Adr[0], I_O_Adr[1], ~I_O_Adr[2], I_O_Adr[3]);  // AND_Gate
  // Probe on controlled_buffer_12_out
  Shifter #(.shift("lr")) shifter_1 (.in(controlled_buffer_12_out), .\dist (3'b011), .out(shifter_1_out));
  Decoder #(.disabled(0)) decoder_4 (.out0(decoder_4_out0), .sel(Rd_Wr), .en(IO_FA_out));  // open: out1
  // Probe on shifter_1_out
  Comparator #(.mode("unsigned")) comparator_1 (
    .a(controlled_buffer_12_out), .b(8'h7f), .gt(comparator_1_gt), .eq(comparator_1_eq), .lt(comparator_1_lt));
  // Probe on shifter_1_out[3:0]
  or or_4 (or_4_out, comparator_1_gt, comparator_1_eq);
  // Probe on shifter_1_out[7:4]
  Decoder #(.select(4), .disabled(0)) decoder_5 (
    .out0(decoder_5_out0[0]), .out1(decoder_5_out0[1]), .out2(decoder_5_out0[2]), .out3(decoder_5_out0[3]),
    .out4(decoder_5_out0[4]), .out5(decoder_5_out0[5]), .out6(decoder_5_out0[6]), .out7(decoder_5_out0[7]),
    .out8(decoder_5_out0[8]), .out9(decoder_5_out0[9]), .out10(decoder_5_out0[10]),
    .out11(decoder_5_out0[11]), .out12(decoder_5_out0[12]), .out13(decoder_5_out0[13]),
    .out14(decoder_5_out0[14]), .out15(decoder_5_out0[15]), .sel(shifter_1_out[3:0]), .en(comparator_1_lt));
  Decoder #(.select(4), .disabled(0)) decoder_6 (
    .out0(decoder_6_out0[0]), .out1(decoder_6_out0[1]), .out2(decoder_6_out0[2]), .out3(decoder_6_out0[3]),
    .out4(decoder_6_out0[4]), .out5(decoder_6_out0[5]), .out6(decoder_6_out0[6]), .out7(decoder_6_out0[7]),
    .out8(decoder_6_out0[8]), .out9(decoder_6_out0[9]), .out10(decoder_6_out0[10]),
    .out11(decoder_6_out0[11]), .out12(decoder_6_out0[12]), .out13(decoder_6_out0[13]),
    .out14(decoder_6_out0[14]), .out15(decoder_6_out0[15]), .sel(shifter_1_out[7:4]), .en(or_4_out));
  // Probe on {decoder_6_out0, decoder_5_out0}
  Shifter #(.width(32)) shifter_2 (.in({decoder_6_out0, decoder_5_out0}), .\dist (5'b00001), .out(shifter_2_out));
  Shifter #(.width(32), .shift("lr")) shifter_3 (
    .in({decoder_6_out0, decoder_5_out0}), .\dist (5'b00001), .out(shifter_3_out));
  assign LPad = {decoder_6_out0, decoder_5_out0} | shifter_3_out | shifter_2_out;  // OR_Gate or_5, 32 bits wide
  assign controlled_buffer_13_out = decoder_7_out0 ? I_O_Dat : 8'bz;  // Controlled_Buffer controlled_buffer_13
  and IO_FB (IO_FB_out, I_O_Adr[0], I_O_Adr[0], I_O_Adr[1], ~I_O_Adr[2], I_O_Adr[3]);  // AND_Gate
  // Probe on controlled_buffer_13_out
  Shifter #(.shift("lr")) shifter_4 (.in(controlled_buffer_13_out), .\dist (3'b011), .out(shifter_4_out));
  Decoder #(.disabled(0)) decoder_7 (.out0(decoder_7_out0), .sel(Rd_Wr), .en(IO_FB_out));  // open: out1
  // Probe on shifter_4_out
  Comparator #(.mode("unsigned")) comparator_2 (
    .a(controlled_buffer_13_out), .b(8'h7f), .gt(comparator_2_gt), .eq(comparator_2_eq), .lt(comparator_2_lt));
  // Probe on shifter_4_out[3:0]
  or or_6 (or_6_out, comparator_2_gt, comparator_2_eq);
  // Probe on shifter_4_out[7:4]
  Decoder #(.select(4), .disabled(0)) decoder_8 (
    .out0(decoder_8_out0[0]), .out1(decoder_8_out0[1]), .out2(decoder_8_out0[2]), .out3(decoder_8_out0[3]),
    .out4(decoder_8_out0[4]), .out5(decoder_8_out0[5]), .out6(decoder_8_out0[6]), .out7(decoder_8_out0[7]),
    .out8(decoder_8_out0[8]), .out9(decoder_8_out0[9]), .out10(decoder_8_out0[10]),
    .out11(decoder_8_out0[11]), .out12(decoder_8_out0[12]), .out13(decoder_8_out0[13]),
    .out14(decoder_8_out0[14]), .out15(decoder_8_out0[15]), .sel(shifter_4_out[3:0]), .en(comparator_2_lt));
  Decoder #(.select(4), .disabled(0)) decoder_9 (
    .out0(decoder_9_out0[0]), .out1(decoder_9_out0[1]), .out2(decoder_9_out0[2]), .out3(decoder_9_out0[3]),
    .out4(decoder_9_out0[4]), .out5(decoder_9_out0[5]), .out6(decoder_9_out0[6]), .out7(decoder_9_out0[7]),
    .out8(decoder_9_out0[8]), .out9(decoder_9_out0[9]), .out10(decoder_9_out0[10]),
    .out11(decoder_9_out0[11]), .out12(decoder_9_out0[12]), .out13(decoder_9_out0[13]),
    .out14(decoder_9_out0[14]), .out15(decoder_9_out0[15]), .sel(shifter_4_out[7:4]), .en(or_6_out));
  // Probe on {decoder_9_out0, decoder_8_out0}
  Shifter #(.width(32)) shifter_5 (.in({decoder_9_out0, decoder_8_out0}), .\dist (5'b00001), .out(shifter_5_out));
  Shifter #(.width(32), .shift("lr")) shifter_6 (
    .in({decoder_9_out0, decoder_8_out0}), .\dist (5'b00001), .out(shifter_6_out));
  assign RPad = {decoder_9_out0, decoder_8_out0} | shifter_6_out | shifter_5_out;  // OR_Gate or_7, 32 bits wide
  assign {controlled_buffer_14_out, LScore} = decoder_10_out0 ? I_O_Dat : 8'bz;  // Controlled_Buffer controlled_buffer_14
  Hex_Digit_Display hex_digit_display_5 (.value(LScore));  // open: dp
  and IO_FC (IO_FC_out, I_O_Adr[0], ~I_O_Adr[0], ~I_O_Adr[1], I_O_Adr[2], I_O_Adr[3]);  // AND_Gate
  Decoder #(.disabled(0)) decoder_10 (.out0(decoder_10_out0), .sel(Rd_Wr), .en(IO_FC_out));  // open: out1
  assign {controlled_buffer_15_out, RScore} = decoder_11_out0 ? I_O_Dat : 8'bz;  // Controlled_Buffer controlled_buffer_15
  Hex_Digit_Display hex_digit_display_6 (.value(RScore));  // open: dp
  and IO_FD (IO_FD_out, I_O_Adr[0], I_O_Adr[0], ~I_O_Adr[1], I_O_Adr[2], I_O_Adr[3]);  // AND_Gate
  Decoder #(.disabled(0)) decoder_11 (.out0(decoder_11_out0), .sel(Rd_Wr), .en(IO_FD_out));  // open: out1
  assign controlled_buffer_16_out = decoder_12_out0 ? I_O_Dat : 8'bz;  // Controlled_Buffer controlled_buffer_16
  // Probe on controlled_buffer_16_out
  and IO_FE (IO_FE_out, I_O_Adr[0], ~I_O_Adr[0], I_O_Adr[1], I_O_Adr[2], I_O_Adr[3]);  // AND_Gate
  Decoder #(.disabled(0)) decoder_12 (.out0(decoder_12_out0), .sel(Rd_Wr), .en(IO_FE_out));  // open: out1
  // Probe on shifter_7_out
  Shifter #(.shift("lr")) shifter_7 (.in(controlled_buffer_16_out), .\dist (3'b011), .out(shifter_7_out));
  // Probe on shifter_7_out[3:0]
  Comparator #(.mode("unsigned")) comparator_3 (
    .a(controlled_buffer_16_out), .b(8'h7f), .gt(comparator_3_gt), .eq(comparator_3_eq), .lt(comparator_3_lt));
  // Probe on shifter_7_out[7:4]
  Decoder #(.select(4), .disabled(0)) decoder_13 (
    .out0(BallX[0]), .out1(BallX[1]), .out2(BallX[2]), .out3(BallX[3]), .out4(BallX[4]), .out5(BallX[5]),
    .out6(BallX[6]), .out7(BallX[7]), .out8(BallX[8]), .out9(BallX[9]), .out10(BallX[10]), .out11(BallX[11]),
    .out12(BallX[12]), .out13(BallX[13]), .out14(BallX[14]), .out15(BallX[15]), .sel(shifter_7_out[3:0]),
    .en(comparator_3_lt));
  Decoder #(.select(4), .disabled(0)) decoder_14 (
    .out0(BallX[16]), .out1(BallX[17]), .out2(BallX[18]), .out3(BallX[19]), .out4(BallX[20]),
    .out5(BallX[21]), .out6(BallX[22]), .out7(BallX[23]), .out8(BallX[24]), .out9(BallX[25]),
    .out10(BallX[26]), .out11(BallX[27]), .out12(BallX[28]), .out13(BallX[29]), .out14(BallX[30]),
    .out15(BallX[31]), .sel(shifter_7_out[7:4]), .en(or_8_out));
  or or_8 (or_8_out, comparator_3_gt, comparator_3_eq);
  // Probe on BallX
  assign controlled_buffer_17_out = decoder_15_out0 ? I_O_Dat : 8'bz;  // Controlled_Buffer controlled_buffer_17
  and IO_FF (IO_FF_out, I_O_Adr[0], I_O_Adr[0], I_O_Adr[1], I_O_Adr[2], I_O_Adr[3]);
  // Probe on controlled_buffer_17_out
  Shifter #(.shift("lr")) shifter_8 (.in(controlled_buffer_17_out), .\dist (3'b011), .out(shifter_8_out));
  Decoder #(.disabled(0)) decoder_15 (.out0(decoder_15_out0), .sel(Rd_Wr), .en(IO_FF_out));  // open: out1
  // Probe on shifter_8_out
  Comparator #(.mode("unsigned")) comparator_4 (
    .a(controlled_buffer_17_out), .b(8'h7f), .gt(comparator_4_gt), .eq(comparator_4_eq), .lt(comparator_4_lt));
  // Probe on shifter_8_out[3:0]
  or or_9 (or_9_out, comparator_4_gt, comparator_4_eq);
  // Probe on shifter_8_out[7:4]
  Decoder #(.select(4), .disabled(0)) decoder_16 (
    .out0(BallY[0]), .out1(BallY[1]), .out2(BallY[2]), .out3(BallY[3]), .out4(BallY[4]), .out5(BallY[5]),
    .out6(BallY[6]), .out7(BallY[7]), .out8(BallY[8]), .out9(BallY[9]), .out10(BallY[10]), .out11(BallY[11]),
    .out12(BallY[12]), .out13(BallY[13]), .out14(BallY[14]), .out15(BallY[15]), .sel(shifter_8_out[3:0]),
    .en(comparator_4_lt));
  Decoder #(.select(4), .disabled(0)) decoder_17 (
    .out0(BallY[16]), .out1(BallY[17]), .out2(BallY[18]), .out3(BallY[19]), .out4(BallY[20]),
    .out5(BallY[21]), .out6(BallY[22]), .out7(BallY[23]), .out8(BallY[24]), .out9(BallY[25]),
    .out10(BallY[26]), .out11(BallY[27]), .out12(BallY[28]), .out13(BallY[29]), .out14(BallY[30]),
    .out15(BallY[31]), .sel(shifter_8_out[7:4]), .en(or_9_out));
  // Probe on BallY
  // also tied to GND on the sheet: {controlled_buffer_12_out[3], controlled_buffer_12_out[5], controlled_buffer_12_out[6], controlled_buffer_12_out[7], controlled_buffer_13_out[3], controlled_buffer_13_out[5], controlled_buffer_13_out[6], controlled_buffer_13_out[7], controlled_buffer_16_out[3], controlled_buffer_16_out[5], controlled_buffer_16_out[6], controlled_buffer_16_out[7], controlled_buffer_17_out[3], controlled_buffer_17_out[5], controlled_buffer_17_out[6], controlled_buffer_17_out[7]}
  // also tied to VCC on the sheet: {controlled_buffer_12_out[0], controlled_buffer_12_out[1], controlled_buffer_12_out[2], controlled_buffer_12_out[4], controlled_buffer_13_out[0], controlled_buffer_13_out[1], controlled_buffer_13_out[2], controlled_buffer_13_out[4], controlled_buffer_16_out[0], controlled_buffer_16_out[1], controlled_buffer_16_out[2], controlled_buffer_16_out[4], controlled_buffer_17_out[0], controlled_buffer_17_out[1], controlled_buffer_17_out[2], controlled_buffer_17_out[4]}

  // Other names for the same wires on the sheet: I_O_Sel = I_O_Adr[0]

  // Notes on the sheet:
  //   Keyboard Input-W,S,x
  //   contents of rom_1 (hex, n*v repeats v):
  //   d2 f8 ba d3 fa ae d4
  //   Test
  //   Keyboard input -F8
  //   FA-Left Paddle
  //   FB-Right Paddle
  //   FC - Left Score
  //   FD - Right Score
  //   FE - Ball X
  //   FF - Ball Y
endmodule

module CDM8 (
);

  wire and_2_out, cdm_8_1_p2, cdm_8_1_p4, cdm_8_1_p5, cdm_8_1_p6, cdm_8_1_p7, cdm_8_1_p8, cdm_8_1_p9,
       cdm_8_1_p10, Clk, decoder_1_out0, decoder_1_out1, decoder_1_out2, decoder_1_out3, decoder_1_out4,
       decoder_1_out5, decoder_1_out6, decoder_1_out7, I_O_Sel, not_1_out, not_2_out, Rd_Wr, Reset;
  wire [2:0] I_O_Adr;
  wire [7:0] cdm_8_1_p13, cdm_8_1_p14, I_O_Dat;
  wire [7:3] cdm_8_1_p12;

  // Probe on cdm_8_1_p2
  Button button_1 (.out(Reset));
  Clock clock_1 (.out(Clk));
  Decoder #(.select(3)) decoder_1 (
    .out0(decoder_1_out0), .out1(decoder_1_out1), .out2(decoder_1_out2), .out3(decoder_1_out3),
    .out4(decoder_1_out4), .out5(decoder_1_out5), .out6(decoder_1_out6), .out7(decoder_1_out7),
    .sel(I_O_Adr), .en(I_O_Sel));
  // Probe on cdm_8_1_p6
  // Probe on cdm_8_1_p4
  // Probe on cdm_8_1_p5
  Keyboard keyboard_1 ();  // open: clk, re, clr, avail, data
  LED led_1 (.in(decoder_1_out0));
  LED led_2 (.in(decoder_1_out1));
  LED led_3 (.in(decoder_1_out2));
  LED led_4 (.in(decoder_1_out3));
  // Probe on cdm_8_1_p7
  // Probe on cdm_8_1_p8
  LED led_5 (.in(decoder_1_out4));
  LED led_6 (.in(decoder_1_out5));
  LED led_7 (.in(decoder_1_out6));
  LED led_8 (.in(decoder_1_out7));
  // Probe on cdm_8_1_p9
  not not_1 (not_1_out, Rd_Wr);
  // CdM_8 cdm_8_1: pin names not known; wires that end beside it: Clk, cdm_8_1_p2, Reset, cdm_8_1_p4, cdm_8_1_p5, cdm_8_1_p6, cdm_8_1_p7, cdm_8_1_p8, cdm_8_1_p9, cdm_8_1_p10, Rd_Wr, {cdm_8_1_p12, I_O_Adr}, cdm_8_1_p13, cdm_8_1_p14, Rd_Wr
  assign I_O_Dat = not_1_out ? cdm_8_1_p13 : 8'bz;  // Controlled_Buffer controlled_buffer_1
  assign cdm_8_1_p14 = Rd_Wr ? I_O_Dat : 8'bz;  // Controlled_Buffer controlled_buffer_2
  not not_2 (not_2_out, I_O_Sel);
  and and_1 (I_O_Sel, cdm_8_1_p10, cdm_8_1_p12[7], cdm_8_1_p12[6], cdm_8_1_p12[5], cdm_8_1_p12[4], cdm_8_1_p12[3]);
  // Probe on {cdm_8_1_p12, I_O_Adr}
  and and_2 (and_2_out, cdm_8_1_p10, not_2_out);
  // Probe on I_O_Dat
  RAM ram_1 (.addr({cdm_8_1_p12, I_O_Adr}), .data(I_O_Dat), .sel(and_2_out), .clk(Clk), .ld(Rd_Wr));  // open: clr
endmodule
