// Logisim project TvTennis.circ as structural Verilog: 2 circuits, main circuit main
module main (
  input  [31:0] in_1
);

  wire Clock, DOWN_2_out, DOWN_out, RESET_2_out, RESET_out, UP_2_out, UP_out;
  wire [1:0] button_1_out;
  wire [31:0] multiplexer_1_out, paddle_shift_1_out_4, paddle_shift_2_out_4, register_1_q, shifter_1_out,
       shifter_2_out;

  Button RESET (.out(RESET_out));
  Button UP (.out(UP_out));
  Button DOWN (.out(DOWN_out));
  Hex_Digit_Display hex_digit_display_1 ();  // open: value, dp
  DotMatrix #(.matrixcols(32), .matrixrows(32)) dotmatrix_1 (
    .col0(paddle_shift_1_out_4), .col31(paddle_shift_2_out_4));  // open: col1, col2, col3, col4, col5, col6, col7, col8, col9, col10, col11, col12, col13, col14, col15, col16, col17, col18, col19, col20, col21, col22, col23, col24, col25, col26, col27, col28, col29, col30
  Paddle_Shift paddle_shift_1 (.Up(UP_out), .Reset(RESET_out), .Down(DOWN_out), .out_4(paddle_shift_1_out_4));
  Hex_Digit_Display hex_digit_display_2 ();  // open: value, dp
  Paddle_Shift paddle_shift_2 (.Up(UP_2_out), .Reset(RESET_2_out), .Down(DOWN_2_out), .out_4(paddle_shift_2_out_4));
  Button UP_2 (.out(UP_2_out));
  Button DOWN_2 (.out(DOWN_2_out));
  Button RESET_2 (.out(RESET_2_out));
  Shifter #(.width(32)) shifter_1 (.in(register_1_q), .\dist (5'b00001), .out(shifter_1_out));
  Multiplexer #(.select(2), .width(32), .enable("false")) multiplexer_1 (
    .in0(register_1_q), .in1(shifter_1_out), .in2(shifter_2_out), .out(multiplexer_1_out), .sel(button_1_out));  // open: in3
  Shifter #(.width(32), .shift("lr")) shifter_2 (.in(register_1_q), .\dist (5'b00001), .out(shifter_2_out));
  Button button_1 (.out(button_1_out[0]));
  Button button_2 (.out(button_1_out[1]));
  Register #(.width(32)) register_1 (.D(multiplexer_1_out), .Q(register_1_q), .clk(Clock));  // open: en, clr
endmodule

module Paddle_Shift (
  input  Up,
  input  Reset,
  input  Down,
  output [31:0] out_4
);

  wire clock_1_out, not_1_out;
  wire [31:0] controlled_buffer_1_out, multiplexer_1_out, shifter_1_out, shifter_2_out;

  Shifter #(.width(32)) shifter_1 (.in(out_4), .\dist (5'b00001), .out(shifter_1_out));
  Shifter #(.width(32), .shift("lr")) shifter_2 (.in(out_4), .\dist (5'b00001), .out(shifter_2_out));
  Multiplexer #(.select(2), .width(32), .enable("false")) multiplexer_1 (
    .in0(out_4), .in1(shifter_1_out), .in2(shifter_2_out), .out(multiplexer_1_out), .sel({Down, Up}));  // open: in3
  assign controlled_buffer_1_out = not_1_out ? multiplexer_1_out : 32'bz;  // Controlled_Buffer controlled_buffer_1
  not not_1 (not_1_out, Reset);
  Register #(.width(32)) register_1 (.D(controlled_buffer_1_out), .Q(out_4), .clk(clock_1_out));  // open: en, clr
  Clock clock_1 (.out(clock_1_out));
  assign controlled_buffer_1_out = Reset ? 32'h3c000 : 32'bz;  // Controlled_Buffer controlled_buffer_2
endmodule
